# Fritzing sketch ESP-Arduino_programing_board (saved by Fritzing 0.9.0b)
breadboards: 1

parts:
  Part2 = Logic Level Converter
  S1 = SWITCH-DPDT [package=os]
  S2 = SWITCH-DPDT [package=os]
  Part3 = FTDI Basic Programmer
  Part1 = Arduino Uno (Rev3)
  Program = Pushbutton [package="[THT]"]
  Reset = Pushbutton [package="[THT]"]

nets:
  N1: Part2.TX2_LV, S2.1
  N2: Part2.RX2_LV, S2.6
  GND: Part2.GND, Part3.GND, Part1.GND, Program.Pin_1, Program.Pin_2, Reset.Pin_1, Reset.Pin_2
  N3: Part2.LV, Part1.3V3
  N4: Part2.HV, Part3.POWER, Part1.5V
  N5: Part2.RX2_HV, S1.4
  N6: Part2.TX2_HV, S1.3
  N7: S1.1, S2.3, Part3.TXO
  N8: S1.2, Part1.D1/TX
  N9: S1.5, Part1.D0/RX
  N10: S1.6, S2.4, Part3.RXI
  N11: Program.Pin_3, Program.Pin_4
  N12: Reset.Pin_3, Reset.Pin_4

notes:
  ESP8266
